# Fritzing sketch fritzing connection drawing (saved by Fritzing 0.9.3b)
breadboards: 1

parts:
  Part1 = Arduino Uno (Rev3) - ICSP
  Reg1 = DC-DC CONVERTER [part_number=80633 package=dc-dc_converter]
  VCC2 = Battery
  VCC3 = Battery block 9V
  GY3 = MPU-6050 Board GY-521 [form="♀ (female)" package=THT]
  S1 = H-Bridge with L298N
  M1 = DC Motor
  M2 = DC Motor
  Raspberry_Pi_1 = Raspberry Pi 3 [part_number=RPI-3-V1.2]
  JP1 = USB_MICROB_PLUG [package=micro-b-ra-smt]

nets:
  N1: Part1.A4/SDA, GY3.pin4
  N2: Part1.A5/SCL, GY3.pin3
  N3: Part1.D8, S1.IN3
  N4: Part1.D12/MISO, S1.IN4
  N5: Part1.D0/RX, Raspberry_Pi_1.GPIO14
  N6: Part1.D2, GY3.pin8
  N7: Part1.D3_PWM, S1.ENA
  N8: Part1.D4, S1.IN1
  N9: Part1.D5_PWM, S1.ENB
  N10: Part1.D7, S1.IN2
  N11: Part1.5V, GY3.pin1
  GND: Part1.GND, Reg1.IN-, VCC2.-, S1.GND
  VIN: Part1.VIN, Reg1.IN+, VCC3.+, S1.12V
  N12: Reg1.OUT-, JP1.D+
  N13: Reg1.OUT+, JP1.VCC
  N14: VCC2.+, VCC3.-
  N15: S1.M1-01, M2.pin_1
  N16: S1.M1-02, M2.pin_2
  N17: S1.M2-01, M1.pin_2
  N18: S1.M2-02, M1.pin_1

custom parts:
  DC-DC CONVERTER: WYHP 5A constant current/voltage manufactured by Shenzhen Weiyapuhua Technology Co., Ltd
  MPU-6050 Board GY-521: Acelerometro y Giroscopio MPU-6050 Board GY-521
  H-Bridge with L298N: h-bridge
